# Fritzing sketch gcp (saved by Fritzing 0.9.4)

parts:
  Brew_Light = LED - 3mm [color="Red (633nm)" package="3 mm [THT]"]
  Steam_Light = LED - 3mm [color="Red (633nm)" package="3 mm [THT]"]
  OLED = Adafruit OLED FeatherWing [part_number="Adafruit #2900"]
  PT100_Amplifier = Adafruit MAX31865 RTD Sensor Breakout [part_number="Adafruit #3328"]
  Controller = Adafruit HUZZAH32 ESP32 Feather [part_number="Adafruit #3405"]
  Relay = Screw terminal - 2 pins [package=THT]

nets:
  N1: Brew_Light.cathode, Steam_Light.cathode, Relay.pin2
  N2: Brew_Light.anode, Controller.IO12_A11
  N3: Steam_Light.anode, Controller.IO13_A12
  N4: OLED.MISO, PT100_Amplifier.SDO, Controller.MISO
  N5: OLED.MOSI, PT100_Amplifier.SDI, Controller.MOSI
  N6: OLED.SCK, PT100_Amplifier.SCLK, Controller.SCK
  N7: OLED.F, PT100_Amplifier.CS, Controller.A5_IO4
  N8: OLED.USB, PT100_Amplifier.VIN, Controller.VBUS
  N9: OLED.J, Controller.IO15_A8
  N10: OLED.I, Controller.IO32_A7
  N11: OLED.H, Controller.IO14_A6
  N12: OLED.SCL, Controller.SCL
  N13: OLED.SDA, Controller.SDA
  GND: OLED.GND, PT100_Amplifier.GND, Controller.GND
  N14: Controller.IO27_A10, Relay.pin1

custom parts:
  Adafruit OLED FeatherWing: This is the FeatherWing OLED: it adds a 128x32 monochrome OLED plus 3 user buttons to any Feather main board. These displays are small, only about 1" diagonal, but very readable due to the high contrast of an OLED display. This screen is made of 128x32 individual white OLED pixels and because the display makes its own light, no backlight is required. This reduces the power required to run the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
  Adafruit MAX31865 RTD Sensor Breakout: For precision temperature sensing, nothing beats a Platinum RTD. Resistance temperature detectors (RTDs) are temperature sensors that contain a resistor that changes resistance value as its temperature changes, basically a kind of thermistor. In this sensor, the resistor is actually a small strip of Platinum with a resistance of 100 ohms at 0°C, thus the name PT100. Compared to most NTC/PTC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
